// Logisim project LAB1-ETY-2206081534-AkmalRamadhan.circ as structural Verilog
module Rangkaian_1 (
  input  A,
  input  B,
  output A_prime_B_prime,
  output A_prime_B,
  output AB_prime,
  output AB
);

  wire not_1_out, not_2_out, not_3_out, not_4_out;

  not not_1 (not_1_out, A);
  not not_2 (not_2_out, B);
  not not_3 (not_3_out, A);
  not not_4 (not_4_out, B);
  and and_1 (A_prime_B_prime, not_1_out, not_2_out);
  and and_2 (A_prime_B, not_3_out, B);
  and and_3 (AB_prime, A, not_4_out);
  and and_4 (AB, A, B);

  // Notes on the sheet:
  //   LAB1 - ETY - 2206081534 - Akmal Ramadhan
endmodule

module Rangkaian_2 (
  input  A,
  input  B,
  input  X,
  input  Y,
  input  Z,
  output A_prime_B_prime_X___A_prime_B_X_Y__prime___AB_prime_Y_Z____ABZ
);

  wire A_prime_B_prime_X_out, A_prime_B_X_Y__prime_out, AB_prime_X_Y_out, ABZ_out, not_1_out, not_2_out,
       not_3_out, not_4_out, not_5_out, or_1_out, or_2_out;

  or or_1 (or_1_out, X, Y);
  not not_1 (not_1_out, or_1_out);
  or or_2 (or_2_out, Y, Z);
  not not_2 (not_2_out, A);
  and A_prime_B_prime_X (A_prime_B_prime_X_out, not_2_out, X, not_3_out);
  not not_3 (not_3_out, B);
  not not_4 (not_4_out, A);
  and A_prime_B_X_Y__prime (A_prime_B_X_Y__prime_out, not_4_out, not_1_out, B);
  and AB_prime_X_Y (AB_prime_X_Y_out, A, or_2_out, not_5_out);
  not not_5 (not_5_out, B);
  and ABZ (ABZ_out, A, Z, B);
  or or_3 (A_prime_B_prime_X___A_prime_B_X_Y__prime___AB_prime_Y_Z____ABZ, A_prime_B_prime_X_out, A_prime_B_X_Y__prime_out, AB_prime_X_Y_out, ABZ_out);

  // Notes on the sheet:
  //   LAB1 - ETY - 2206081534 - Akmal Ramadhan
endmodule
