// Logisim project LAB2-ETY-2206081534-AkmalRamadhan.circ as structural Verilog: 2 circuits, main circuit Sebelum Dioptimasi
module Sebelum_Dioptimasi (
  input  W,
  input  X,
  input  Y,
  input  Z,
  output O_W_X_Y_Z
);

  wire m1_out, m2_out, m3_out, m4_out, m6_out, m8_out, m12_out, not_1_out, not_2_out, not_3_out, not_4_out;

  not not_1 (not_1_out, W);
  not not_2 (not_2_out, X);
  not not_3 (not_3_out, Y);
  not not_4 (not_4_out, Z);
  and m1 (m1_out, not_1_out, not_2_out, not_3_out, Z);
  and m2 (m2_out, not_1_out, not_2_out, Y, not_4_out);
  and m3 (m3_out, not_1_out, not_2_out, Y, Z);
  and m4 (m4_out, not_1_out, X, not_3_out, not_4_out);
  and m6 (m6_out, not_1_out, X, Y, not_4_out);
  and m8 (m8_out, W, not_2_out, not_3_out, not_4_out);
  and m12 (m12_out, W, X, not_3_out, not_4_out);
  or or_1 (O_W_X_Y_Z, m1_out, m2_out, m3_out, m4_out, m6_out, m8_out, m12_out);

  // Notes on the sheet:
  //   Sum of Minterms (SOM)
endmodule

module Sesudah_Dioptimasi (
  input  W,
  input  X,
  input  Y,
  input  Z,
  output O_W_X_Y_Z
);

  wire not_1_out, not_2_out, not_3_out, not_4_out, W_prime_X_prime_Y_out, W_prime_X_prime_Z_out,
       W_prime_XZ_prime_out, WY_prime_Z_prime_out;

  not not_1 (not_1_out, W);
  not not_2 (not_2_out, Y);
  not not_3 (not_3_out, X);
  not not_4 (not_4_out, Z);
  and W_prime_X_prime_Z (W_prime_X_prime_Z_out, not_1_out, not_3_out, Z);
  and W_prime_X_prime_Y (W_prime_X_prime_Y_out, not_1_out, not_3_out, Y);
  and W_prime_XZ_prime (W_prime_XZ_prime_out, not_1_out, X, not_4_out);
  and WY_prime_Z_prime (WY_prime_Z_prime_out, W, not_2_out, not_4_out);
  or or_1 (O_W_X_Y_Z, W_prime_X_prime_Z_out, W_prime_X_prime_Y_out, W_prime_XZ_prime_out, WY_prime_Z_prime_out);

  // Notes on the sheet:
  //   Optimized
  //   Sum of Minterms (SOM)
endmodule
