// Logisim project LAB3-ETY-2206081534-AkmalRamadhan.circ as structural Verilog: 3 circuits, main circuit main
module main (
  input  MSB,
  input  LSB,
  input  s1,
  input  s0,
  output Output
);

  wire n2_to_4_decoder_1__00, n2_to_4_decoder_1__01, n2_to_4_decoder_1__10, n2_to_4_decoder_1__11;

  _2_to_4_Decoder u_2_to_4_decoder_1 (
    .A____MSB(MSB), .B____LSB(LSB), ._00(n2_to_4_decoder_1__00), ._01(n2_to_4_decoder_1__01),
    ._10(n2_to_4_decoder_1__10), ._11(n2_to_4_decoder_1__11));
  Multiplexer_Standard_4_Bit multiplexer_standard_4_bit_1 (
    ._00(n2_to_4_decoder_1__00), ._01(n2_to_4_decoder_1__01), ._10(n2_to_4_decoder_1__10),
    ._11(n2_to_4_decoder_1__11), .s1(s1), .s0(s0), .Output(Output));

  // Notes on the sheet:
  //   Input
  //   2-4 Dec
  //   LAB3 - ETY - 2206081534 - Akmal Ramadhan
  //   Multiplexer 4 Bit
  //   Selector
endmodule

module _2_to_4_Decoder (
  input  A____MSB,
  input  B____LSB,
  output _00,
  output _01,
  output _10,
  output _11
);

  wire not_1_out, not_2_out;

  not not_1 (not_1_out, A____MSB);
  not not_2 (not_2_out, B____LSB);
  and and_1 (_00, A____MSB, B____LSB);
  and and_2 (_01, A____MSB, not_2_out);
  and and_3 (_10, not_1_out, B____LSB);
  and and_4 (_11, not_1_out, not_2_out);

  // Notes on the sheet:
  //   2 to 4 Decoder
  //   A'B'
endmodule

module Multiplexer_Standard_4_Bit (
  input  _00,
  input  _01,
  input  _10,
  input  _11,
  input  s1,
  input  s0,
  output Output
);

  wire and_1_out, and_2_out, and_3_out, and_4_out, and_5_out, and_6_out, and_7_out, and_8_out, not_1_out,
       not_2_out;

  not not_1 (not_1_out, s1);
  and and_1 (and_1_out, not_1_out, not_2_out);
  not not_2 (not_2_out, s0);
  and and_2 (and_2_out, s1, not_2_out);
  and and_3 (and_3_out, not_1_out, s0);
  and and_4 (and_4_out, s1, s0);
  and and_5 (and_5_out, _00, and_1_out);
  and and_6 (and_6_out, _01, and_3_out);
  and and_7 (and_7_out, _10, and_2_out);
  and and_8 (and_8_out, _11, and_4_out);
  or or_1 (Output, and_5_out, and_6_out, and_7_out, and_8_out);

  // Notes on the sheet:
  //   Multiplexer Standard 4 Bit
endmodule
