// Logisim project LAB4-ETY-2206081534-AkmalRamadhan.circ as structural Verilog: 4 circuits, main circuit Full Adder
// FA
module Full_Adder (
  input  Y,
  input  X,
  input  Z,
  output C,
  output S
);

  wire and_1_out, and_2_out, xor_2_out;

  and and_1 (and_1_out, Z, xor_2_out);
  or or_1 (C, and_2_out, and_1_out);
  and and_2 (and_2_out, Y, X);
  xor xor_1 (S, Z, xor_2_out);
  xor xor_2 (xor_2_out, Y, X);

  // Notes on the sheet:
  //   Full Adder
  //   LAB4-ETY-2206081534-AkmalRamadhan
  //   HA
  //   HA
endmodule

module Rangkaian_4_bit_parallel_adder (
  input  [3:0] B,
  input  [3:0] A,
  output Overflow,
  output [3:0] S
);

  wire full_adder_1_c, full_adder_2_c, full_adder_3_c, full_adder_4_c;

  Full_Adder full_adder_1 (.C(full_adder_1_c), .Y(B[3]), .X(A[3]), .S(S[3]), .Z(full_adder_2_c));
  xor xor_1 (Overflow, full_adder_2_c, full_adder_1_c);
  Full_Adder full_adder_2 (.C(full_adder_2_c), .Y(B[2]), .X(A[2]), .S(S[2]), .Z(full_adder_4_c));
  Full_Adder full_adder_3 (.C(full_adder_3_c), .Y(B[0]), .X(A[0]), .S(S[0]), .Z(1'b0));
  Full_Adder full_adder_4 (.C(full_adder_4_c), .Y(B[1]), .X(A[1]), .S(S[1]), .Z(full_adder_3_c));

  // Notes on the sheet:
  //   LAB4-ETY-2206081534-AkmalRamadhan
  //   4-bit Parallel Adder
  //   Cin
endmodule

module Rangkaian_peubah (
  input  [3:0] Input,
  output [3:0] Output
);

  wire full_adder_2_c, full_adder_3_c, full_adder_4_c;

  Full_Adder full_adder_1 (.Y(1'b0), .X(Input[3]), .S(Output[3]), .Z(full_adder_2_c));  // open: C
  Full_Adder full_adder_2 (.C(full_adder_2_c), .Y(1'b0), .X(Input[2]), .S(Output[2]), .Z(full_adder_3_c));
  Full_Adder full_adder_3 (.C(full_adder_3_c), .Y(1'b0), .X(Input[1]), .S(Output[1]), .Z(full_adder_4_c));
  Full_Adder full_adder_4 (.C(full_adder_4_c), .Y(1'b0), .X(Input[0]), .S(Output[0]), .Z(Input[3]));

  // Notes on the sheet:
  //   LAB4-ETY-2206081534-AkmalRamadhan
  //   Rangkaian Peubah
endmodule

module Rangkaian_akhir (
  input  [3:0] B,
  input  [3:0] A,
  output Overflow,
  output [3:0] S
);

  wire [3:0] rangkaian_peubah_1_output, rangkaian_peubah_2_output;

  Rangkaian_peubah rangkaian_peubah_1 (.Input(B), .Output(rangkaian_peubah_1_output));
  Rangkaian_4_bit_parallel_adder rangkaian_4_bit_parallel_adder_1 (
    .Overflow(Overflow), .B(rangkaian_peubah_1_output), .A(rangkaian_peubah_2_output), .S(S));
  Rangkaian_peubah rangkaian_peubah_2 (.Input(A), .Output(rangkaian_peubah_2_output));

  // Notes on the sheet:
  //   Rangkaian Akhir
  //   LAB4-ETY-2206081534-AkmalRamadhan
endmodule
