// Logisim project LAB5-ETY-2206081534-AkmalRamadhan.circ as structural Verilog: 1 circuit, main circuit Main Circuit
module Main_Circuit (
  input  X,
  output Y
);

  wire and_1_out, and_2_out, clock_1_out, D0_Y0_q, D1_Y1_q, not_1_out, not_2_out, not_3_out, or_1_out,
       or_2_out;

  Clock clock_1 (.out(clock_1_out));
  not not_1 (not_1_out, X);
  not not_2 (not_2_out, D1_Y1_q);
  not not_3 (not_3_out, D0_Y0_q);
  or or_1 (or_1_out, not_1_out, and_1_out);
  and and_1 (and_1_out, D1_Y1_q, D0_Y0_q);
  or or_2 (or_2_out, X, and_2_out);
  and and_2 (and_2_out, not_2_out, not_3_out);
  and and_3 (Y, D1_Y1_q, X);
  D_Flip_Flop D1_Y1 (.clk(clock_1_out), .D(or_1_out), .Q(D1_Y1_q));  // open: Qn, preset, en, reset
  D_Flip_Flop D0_Y0 (.clk(clock_1_out), .D(or_2_out), .Q(D0_Y0_q));  // open: Qn, preset, en, reset

  // Notes on the sheet:
  //   LAB5-ETY-2206081534-AkmalRamadhan
endmodule
