// Logisim project LAB6-ETY-2206081534-AkmalRamadhan.circ as structural Verilog: 1 circuit, main circuit Main Circuit
module Main_Circuit (
  input  A,
  output O
);

  wire Clock_out, or_1_out, or_2_out, X_q, xnor_1_out, Y_q;

  Clock Clock (.out(Clock_out));
  or or_1 (or_1_out, A, Y_q);
  xnor xnor_1 (xnor_1_out, A, Y_q);
  and and_1 (O, X_q, or_2_out);
  or or_2 (or_2_out, A, Y_q);
  J_K_Flip_Flop X (.J(or_1_out), .clk(Clock_out), .K(or_1_out), .Q(X_q));  // open: Qn, preset, en, reset
  D_Flip_Flop Y (.clk(Clock_out), .D(xnor_1_out), .Q(Y_q));  // open: Qn, preset, en, reset

  // Notes on the sheet:
  //   LAB6-ETY-2206081534-AkmalRamadhan
  //   A+Y
  //   Y'A' + YA
  //   X(A + Y)
endmodule
