// Logisim project LAB7-ETY-2206081534-AkmalRamadhan.circ as structural Verilog: 3 circuits, main circuit Non-Multiplexer
module Non_Multiplexer (
  input  [3:0] B_t,
  input  S1,
  input  S0,
  input  Reset,
  output [3:0] A_t_1
);

  wire Clock_out, input_multiplexer_1_a_t_1, input_multiplexer_2_a_t_1, input_multiplexer_3_a_t_1,
       input_multiplexer_4_a_t_1;

  Input_Multiplexer input_multiplexer_1 (
    .A_t(A_t_1[0]), .B_t(B_t[0]), .S1(S1), .S0(S0), .A_t_1(input_multiplexer_1_a_t_1));
  Input_Multiplexer input_multiplexer_2 (
    .A_t(A_t_1[1]), .B_t(B_t[1]), .S1(S1), .S0(S0), .A_t_1(input_multiplexer_2_a_t_1));
  Input_Multiplexer input_multiplexer_3 (
    .A_t(A_t_1[2]), .B_t(B_t[2]), .S1(S1), .S0(S0), .A_t_1(input_multiplexer_3_a_t_1));
  Input_Multiplexer input_multiplexer_4 (
    .A_t(A_t_1[3]), .B_t(B_t[3]), .S1(S1), .S0(S0), .A_t_1(input_multiplexer_4_a_t_1));
  Clock Clock (.out(Clock_out));
  D_Flip_Flop d_ff_1 (
    .clk(Clock_out), .D(input_multiplexer_1_a_t_1), .Q(A_t_1[0]), .reset(Reset));  // open: Qn, preset, en
  D_Flip_Flop d_ff_2 (
    .clk(Clock_out), .D(input_multiplexer_2_a_t_1), .Q(A_t_1[1]), .reset(Reset));  // open: Qn, preset, en
  D_Flip_Flop d_ff_3 (
    .clk(Clock_out), .D(input_multiplexer_3_a_t_1), .Q(A_t_1[2]), .reset(Reset));  // open: Qn, preset, en
  D_Flip_Flop d_ff_4 (
    .clk(Clock_out), .D(input_multiplexer_4_a_t_1), .Q(A_t_1[3]), .reset(Reset));  // open: Qn, preset, en

  // Notes on the sheet:
  //   LAB7-ETY-2206081534-AkmalRamadhan
  //   A(t)
  //   Gate Cost = 21 * 4 = 84
endmodule

module With_Multiplexer (
  input  [3:0] B_t,
  input  [1:0] Selector,
  input  Reset,
  output [3:0] A_t_1
);

  wire Clock_out;
  wire [3:0] and_1_out, multiplexer_1_out, nor_1_out, or_1_out, xor_1_out;

  assign or_1_out = A_t_1 | B_t;  // OR_Gate or_1, 4 bits wide
  assign and_1_out = A_t_1 & ~B_t;  // AND_Gate and_1, 4 bits wide
  assign xor_1_out = A_t_1 ^ B_t;  // XOR_Gate xor_1, 4 bits wide
  assign nor_1_out = ~(A_t_1 | B_t);  // NOR_Gate nor_1, 4 bits wide
  Multiplexer #(.select(2), .width(4)) multiplexer_1 (
    .in0(or_1_out), .in1(and_1_out), .in2(xor_1_out), .in3(nor_1_out), .out(multiplexer_1_out), .sel(Selector));  // open: en
  Clock Clock (.out(Clock_out));
  D_Flip_Flop d_ff_1 (.clk(Clock_out), .D(multiplexer_1_out[0]), .Q(A_t_1[0]), .reset(Reset));  // open: Qn, preset, en
  D_Flip_Flop d_ff_2 (.clk(Clock_out), .D(multiplexer_1_out[1]), .Q(A_t_1[1]), .reset(Reset));  // open: Qn, preset, en
  D_Flip_Flop d_ff_3 (.clk(Clock_out), .D(multiplexer_1_out[2]), .Q(A_t_1[2]), .reset(Reset));  // open: Qn, preset, en
  D_Flip_Flop d_ff_4 (.clk(Clock_out), .D(multiplexer_1_out[3]), .Q(A_t_1[3]), .reset(Reset));  // open: Qn, preset, en

  // Notes on the sheet:
  //   Gate Cost = (2 + 2 + 6 + 2 + 16) * 4 = 112
  //   LAB7-ETY-2206081534-AkmalRamadhan
  //   A(t)
endmodule

// A(t+1)
module Input_Multiplexer (
  input  A_t,
  input  B_t,
  input  S1,
  input  S0,
  output A_t_1
);

  wire not_1_out, not_2_out, not_3_out, not_4_out, S0_prime_A_B_prime_out, S0_prime_A_prime_B_out,
       S1_prime_A_B_prime_out, S1_prime_S0_prime_A_out, S1_S0_A_prime_B_prime_out;

  not not_1 (not_1_out, S0);
  not not_2 (not_2_out, S1);
  not not_3 (not_3_out, A_t);
  not not_4 (not_4_out, B_t);
  and S0_prime_A_prime_B (S0_prime_A_prime_B_out, not_1_out, not_3_out, B_t);
  and S1_prime_S0_prime_A (S1_prime_S0_prime_A_out, not_2_out, not_1_out, A_t);
  and S1_prime_A_B_prime (S1_prime_A_B_prime_out, not_2_out, A_t, not_4_out);
  and S0_prime_A_B_prime (S0_prime_A_B_prime_out, not_1_out, A_t, not_4_out);
  and S1_S0_A_prime_B_prime (S1_S0_A_prime_B_prime_out, S1, S0, not_4_out, not_3_out);
  or or_1 (A_t_1, S0_prime_A_prime_B_out, S1_prime_S0_prime_A_out, S1_prime_A_B_prime_out, S0_prime_A_B_prime_out, S1_S0_A_prime_B_prime_out);

  // Notes on the sheet:
  //   LAB7-ETY-2206081534-AkmalRamadhan
  //   Gate Cost = 3 * 4 + 4 + 5 = 21
endmodule
