// Logisim project LAB8-ETY-2206081534-AkmalRamadhan.circ as structural Verilog: 3 circuits, main circuit Counter with Parallel Load with Modification
module Main_Circuit (
  input  Reset,
  input  Load,
  input  Count,
  input  inc4,
  input  inc2,
  input  [3:0] Bit_12_15,
  input  [3:0] Bit_8_11,
  input  [3:0] Bit_4_7,
  input  [3:0] Bit_0_3,
  output [3:0] O_12_15,
  output [3:0] O_8_11,
  output [3:0] O_4_7,
  output [3:0] O_0_3
);

  wire Clock_out;

  Clock Clock (.out(Clock_out));
  Hex_Digit_Display hex_digit_display_1 (.value(Bit_12_15));  // open: dp
  Hex_Digit_Display hex_digit_display_2 (.value(Bit_8_11));  // open: dp
  Bigger_Counter Bigger_Counter (
    .Reset(Reset), .Clock(Clock_out), .Load(Load), .Count(Count), .inc4(inc4), .inc2(inc2),
    .Bit_12_15(Bit_12_15), .Bit_8_11(Bit_8_11), .Bit_4_7(Bit_4_7), .Bit_0_3(Bit_0_3), .Output_0_3(O_0_3),
    .Output_4_7(O_4_7), .Output_8_11(O_8_11), .Output_12_15(O_12_15));
  Hex_Digit_Display hex_digit_display_3 (.value(Bit_4_7));  // open: dp
  Hex_Digit_Display hex_digit_display_4 (.value(Bit_0_3));  // open: dp
  Hex_Digit_Display hex_digit_display_5 (.value(O_12_15));  // open: dp
  Hex_Digit_Display hex_digit_display_6 (.value(O_8_11));  // open: dp
  Hex_Digit_Display hex_digit_display_7 (.value(O_4_7));  // open: dp
  Hex_Digit_Display hex_digit_display_8 (.value(O_0_3));  // open: dp

  // Notes on the sheet:
  //   Input
  //   Main Circuit
  //   Output
  //   LAB8-ETY-2206081534-AkmalRamadhan
endmodule

// Parallel Load
module Counter_with_Parallel_Load_with_Modification (
  input  Reset,
  input  Clock,
  input  Load,
  input  Count,
  input  inc4,
  input  inc2,
  input  [3:0] Input,
  output [3:0] Output,
  output Carry_Out
);

  wire and_1_out, and_2_out, and_3_out, and_4_out, and_6_out, and_7_out, and_8_out, and_9_out, and_10_out,
       and_11_out, and_12_out, and_13_out, decoder_1_out0, decoder_1_out1, decoder_1_out2, decoder_1_out3,
       not_1_out, or_1_out, or_2_out, or_3_out, or_4_out, or_5_out, or_6_out, or_7_out, xor_1_out, xor_2_out,
       xor_3_out, xor_4_out;

  not not_1 (not_1_out, Load);
  Decoder #(.select(2), .enable("false")) decoder_1 (
    .out0(decoder_1_out0), .out1(decoder_1_out1), .out2(decoder_1_out2), .out3(decoder_1_out3),
    .sel({inc4, inc2}));
  and and_1 (and_1_out, not_1_out, decoder_1_out0, Count);
  and and_2 (and_2_out, and_1_out, Output[0]);
  or or_1 (or_1_out, decoder_1_out1, and_2_out);
  or or_2 (or_2_out, decoder_1_out3, decoder_1_out2);
  and and_3 (and_3_out, or_1_out, Output[1]);
  or or_3 (or_3_out, or_2_out, and_3_out);
  and and_4 (and_4_out, or_3_out, Output[2]);
  and and_5 (Carry_Out, and_4_out, Output[3]);
  xor xor_1 (xor_1_out, and_1_out, Output[0]);
  xor xor_2 (xor_2_out, or_1_out, Output[1]);
  xor xor_3 (xor_3_out, or_3_out, Output[2]);
  xor xor_4 (xor_4_out, and_4_out, Output[3]);
  and and_6 (and_6_out, Load, Input[0]);
  and and_7 (and_7_out, xor_1_out, not_1_out);
  and and_8 (and_8_out, Load, Input[1]);
  and and_9 (and_9_out, xor_2_out, not_1_out);
  and and_10 (and_10_out, Load, Input[2]);
  and and_11 (and_11_out, xor_3_out, not_1_out);
  and and_12 (and_12_out, Load, Input[3]);
  and and_13 (and_13_out, xor_4_out, not_1_out);
  or or_4 (or_4_out, and_6_out, and_7_out);
  or or_5 (or_5_out, and_8_out, and_9_out);
  or or_6 (or_6_out, and_10_out, and_11_out);
  or or_7 (or_7_out, and_12_out, and_13_out);
  D_Flip_Flop Q0 (.clk(Clock), .D(or_4_out), .Q(Output[0]), .reset(Reset));  // open: Qn, preset, en
  D_Flip_Flop Q1 (.clk(Clock), .D(or_5_out), .Q(Output[1]), .reset(Reset));  // open: Qn, preset, en
  D_Flip_Flop Q2 (.clk(Clock), .D(or_6_out), .Q(Output[2]), .reset(Reset));  // open: Qn, preset, en
  D_Flip_Flop Q3 (.clk(Clock), .D(or_7_out), .Q(Output[3]), .reset(Reset));  // open: Qn, preset, en
  Hex_Digit_Display hex_digit_display_1 (.value(Output));  // open: dp

  // Notes on the sheet:
  //   LAB8-ETY-2206081534-AkmalRamadhan
  //   Counter with Parallel Load with Modification
endmodule

module Bigger_Counter (
  input  Reset,
  input  Clock,
  input  Load,
  input  Count,
  input  inc4,
  input  inc2,
  input  [3:0] Bit_0_3,
  input  [3:0] Bit_4_7,
  input  [3:0] Bit_8_11,
  input  [3:0] Bit_12_15,
  output [3:0] Output_0_3,
  output [3:0] Output_4_7,
  output [3:0] Output_8_11,
  output [3:0] Output_12_15
);

  wire counter_with_parallel_load_with_modification_1_carry_out,
       counter_with_parallel_load_with_modification_2_carry_out,
       counter_with_parallel_load_with_modification_4_carry_out;

  Counter_with_Parallel_Load_with_Modification counter_with_parallel_load_with_modification_1 (
    .Reset(Reset), .Clock(Clock), .Load(Load),
    .Count(counter_with_parallel_load_with_modification_4_carry_out), .inc4(1'b0), .inc2(1'b0),
    .Input(Bit_4_7), .Output(Output_4_7), .Carry_Out(counter_with_parallel_load_with_modification_1_carry_out));
  Counter_with_Parallel_Load_with_Modification counter_with_parallel_load_with_modification_2 (
    .Reset(Reset), .Clock(Clock), .Load(Load),
    .Count(counter_with_parallel_load_with_modification_1_carry_out), .inc4(1'b0), .inc2(1'b0),
    .Input(Bit_8_11), .Output(Output_8_11),
    .Carry_Out(counter_with_parallel_load_with_modification_2_carry_out));
  Counter_with_Parallel_Load_with_Modification counter_with_parallel_load_with_modification_3 (
    .Reset(Reset), .Clock(Clock), .Load(Load),
    .Count(counter_with_parallel_load_with_modification_2_carry_out), .inc4(1'b0), .inc2(1'b0),
    .Input(Bit_12_15), .Output(Output_12_15));  // open: Carry_Out
  Counter_with_Parallel_Load_with_Modification counter_with_parallel_load_with_modification_4 (
    .Reset(Reset), .Clock(Clock), .Load(Load), .Count(Count), .inc4(inc4), .inc2(inc2), .Input(Bit_0_3),
    .Output(Output_0_3), .Carry_Out(counter_with_parallel_load_with_modification_4_carry_out));

  // Notes on the sheet:
  //   Bigger Counter
  //   LAB8-ETY-2206081534-AkmalRamadhan
endmodule
