// Logisim project ETY_TM5_AkmalRamadhan_2206081534.circ as structural Verilog: 5 circuits, main circuit Half Adder
// HA
module Half_Adder (
  input  Y,
  input  X,
  output C,
  output S
);

  and and_1 (C, Y, X);
  xor xor_1 (S, Y, X);
endmodule

// FA
module Full_Adder (
  input  Y,
  input  X,
  input  Z,
  output C,
  output S
);

  wire Half_Adder_2_c, Half_Adder_c, Half_Adder_s;

  Half_Adder Half_Adder (.Y(Y), .X(X), .C(Half_Adder_c), .S(Half_Adder_s));
  Half_Adder Half_Adder_2 (.Y(Z), .X(Half_Adder_s), .C(Half_Adder_2_c), .S(S));
  or or_1 (C, Half_Adder_c, Half_Adder_2_c);
endmodule

module _4_Bit_Adder_Cum_Subtractor (
  input  A3,
  input  A2,
  input  A1,
  input  A0,
  input  B3,
  input  B2,
  input  B1,
  input  B0,
  input  S,
  output S3,
  output S2,
  output S1,
  output S0,
  output Overflow
);

  wire full_adder_1_c, full_adder_2_c, full_adder_3_c, full_adder_4_c, xor_2_out, xor_3_out, xor_4_out,
       xor_5_out;

  xor xor_1 (Overflow, full_adder_1_c, full_adder_2_c);
  xor xor_2 (xor_2_out, B3, S);
  Full_Adder full_adder_1 (.C(full_adder_1_c), .Y(xor_2_out), .X(A3), .S(S3), .Z(full_adder_2_c));
  xor xor_3 (xor_3_out, B2, S);
  Full_Adder full_adder_2 (.C(full_adder_2_c), .Y(xor_3_out), .X(A2), .S(S2), .Z(full_adder_3_c));
  xor xor_4 (xor_4_out, B1, S);
  Full_Adder full_adder_3 (.C(full_adder_3_c), .Y(xor_4_out), .X(A1), .S(S1), .Z(full_adder_4_c));
  xor xor_5 (xor_5_out, B0, S);
  Full_Adder full_adder_4 (.C(full_adder_4_c), .Y(xor_5_out), .X(A0), .S(S0), .Z(S));

  // Notes on the sheet:
  //   C3
  //   C2
  //   C1
  //   C0
endmodule

module _2s_Complement_to_Sign_Magnitude (
  input  in_1,
  input  in_2,
  input  Input,
  input  in_4,
  input  in_5,
  output Cout,
  output S3,
  output S2,
  output S1,
  output S0
);

  wire half_adder_2_c, half_adder_3_c, xor_1_out, xor_2_out, xor_3_out, xor_4_out;

  xor xor_1 (xor_1_out, in_1, in_2);
  xor xor_2 (xor_2_out, xor_1_out, Input);
  Half_Adder half_adder_1 (.Y(xor_2_out), .X(half_adder_2_c), .C(Cout), .S(S2));
  xor xor_3 (xor_3_out, xor_1_out, in_4);
  Half_Adder half_adder_2 (.Y(xor_3_out), .X(half_adder_3_c), .C(half_adder_2_c), .S(S1));
  xor xor_4 (xor_4_out, xor_1_out, in_5);
  Half_Adder half_adder_3 (.Y(xor_4_out), .X(xor_1_out), .C(half_adder_3_c), .S(S0));

  assign S3 = in_2;
endmodule

module Main_Circuit (
  input  [3:0] A,
  input  [3:0] B,
  input  S,
  output Overflow___2s,
  output Overflow___SM,
  output [3:0] Output
);

  wire _4_Bit_Adder_Cum_Subtractor_s0, _4_Bit_Adder_Cum_Subtractor_s1, _4_Bit_Adder_Cum_Subtractor_s2,
       _4_Bit_Adder_Cum_Subtractor_s3;

  _2s_Complement_to_Sign_Magnitude _2s_to_SM (
    .Cout(Overflow___SM), .in_1(Overflow___2s), .in_2(_4_Bit_Adder_Cum_Subtractor_s3),
    .Input(_4_Bit_Adder_Cum_Subtractor_s2), .in_4(_4_Bit_Adder_Cum_Subtractor_s1),
    .in_5(_4_Bit_Adder_Cum_Subtractor_s0), .S3(Output[3]), .S2(Output[2]), .S1(Output[1]), .S0(Output[0]));
  _4_Bit_Adder_Cum_Subtractor _4_Bit_Adder_Cum_Subtractor (
    .B3(B[3]), .A3(A[3]), .B2(B[2]), .A2(A[2]), .B1(B[1]), .A1(A[1]), .B0(B[0]), .A0(A[0]),
    .Overflow(Overflow___2s), .S3(_4_Bit_Adder_Cum_Subtractor_s3), .S2(_4_Bit_Adder_Cum_Subtractor_s2),
    .S1(_4_Bit_Adder_Cum_Subtractor_s1), .S0(_4_Bit_Adder_Cum_Subtractor_s0), .S(S));

  // Notes on the sheet:
  //   Akmal Ramadhan
  //   2206081534
endmodule
