// Logisim project ETY_TM6_AkmalRamadhan_2206081534.circ as structural Verilog: 4 circuits, main circuit Nomor2
module Nomor2 (
  input  Reset,
  input  X,
  output Y
);

  wire and_1_out, and_2_out, and_3_out, and_4_out, and_5_out, and_6_out, and_7_out, and_8_out, and_9_out,
       and_10_out, and_11_out, and_12_out, and_13_out, Clock_out, not_1_out, or_1_out, or_2_out, or_3_out,
       S0_q, S0_qn, S1_q, S1_qn, S2_q, S2_qn;

  Clock Clock (.out(Clock_out));
  not not_1 (not_1_out, X);
  and and_1 (and_1_out, S2_qn, S1_q, X);
  and and_2 (and_2_out, S2_q, S1_qn, S0_qn);
  and and_3 (and_3_out, S2_q, S1_qn, X);
  and and_4 (and_4_out, S2_qn, S1_qn, X);
  and and_5 (and_5_out, S2_qn, S0_q, not_1_out);
  and and_6 (and_6_out, S2_q, S1_q);
  and and_7 (and_7_out, S2_q, S0_qn, not_1_out);
  and and_8 (and_8_out, S2_qn, not_1_out);
  and and_9 (and_9_out, S0_q, not_1_out);
  and and_10 (and_10_out, S1_q, not_1_out);
  and and_11 (and_11_out, S1_q, S0_q);
  and and_12 (and_12_out, S2_q, S0_q, X);
  and and_13 (and_13_out, S2_q, S1_q, not_1_out);
  or or_1 (or_1_out, and_1_out, and_2_out, and_3_out);
  or or_2 (or_2_out, and_4_out, and_5_out, and_6_out, and_7_out);
  or or_3 (or_3_out, and_8_out, and_9_out, and_10_out, and_11_out);
  or or_4 (Y, and_12_out, and_13_out);
  D_Flip_Flop S2 (.clk(Clock_out), .D(or_1_out), .Q(S2_q), .Qn(S2_qn), .reset(Reset));  // open: preset, en
  D_Flip_Flop S1 (.clk(Clock_out), .D(or_2_out), .Q(S1_q), .Qn(S1_qn), .reset(Reset));  // open: preset, en
  D_Flip_Flop S0 (.clk(Clock_out), .D(or_3_out), .Q(S0_q), .Qn(S0_qn), .reset(Reset));  // open: preset, en

  // Notes on the sheet:
  //   ETY-TM6-AkmalRamadhan-2206081534
endmodule

module Nomor3 (
  input  Reset,
  input  X,
  output Y
);

  wire and_1_out, and_2_out, and_3_out, and_4_out, and_5_out, and_6_out, and_7_out, and_8_out, Clock_out,
       not_1_out, or_1_out, S0_q, S0_qn, S1_q, S1_qn, S2_q, S2_qn;

  Clock Clock (.out(Clock_out));
  not not_1 (not_1_out, X);
  and and_1 (and_1_out, S1_qn, not_1_out);
  and and_2 (and_2_out, S1_q, X);
  and and_3 (and_3_out, S2_qn, S1_q, S0_q, not_1_out);
  and and_4 (and_4_out, S2_q, S1_qn);
  and and_5 (and_5_out, S2_q, S0_qn);
  and and_6 (and_6_out, S2_q, X);
  and and_7 (and_7_out, S1_q, S0_q, not_1_out);
  and and_8 (and_8_out, S0_q, not_1_out);
  or or_1 (or_1_out, and_1_out, and_2_out);
  or or_2 (Y, and_3_out, and_4_out, and_5_out, and_6_out);
  J_K_Flip_Flop S2 (
    .J(and_7_out), .clk(Clock_out), .K(and_7_out), .Q(S2_q), .Qn(S2_qn), .reset(Reset));  // open: preset, en
  J_K_Flip_Flop S1 (.J(and_8_out), .clk(Clock_out), .K(S0_q), .Q(S1_q), .Qn(S1_qn), .reset(Reset));  // open: preset, en
  J_K_Flip_Flop S0 (.J(or_1_out), .clk(Clock_out), .K(1'b1), .Q(S0_q), .Qn(S0_qn), .reset(Reset));  // open: preset, en

  // Notes on the sheet:
  //   ETY-TM6-AkmalRamadhan-2206081534
endmodule

module TempCirc (
  input  S2,
  input  S1,
  input  S0,
  input  X,
  output S2T,
  output S1T,
  output S0T,
  output Y
);

  wire and_1_out, and_2_out, and_3_out, and_4_out, and_5_out, and_6_out, and_7_out, and_8_out, and_9_out,
       and_10_out, and_11_out, and_12_out, and_13_out, and_14_out, not_1_out, not_2_out, not_3_out,
       not_4_out, not_5_out, not_6_out, not_7_out, not_8_out, not_9_out, not_10_out, not_11_out, not_12_out,
       not_13_out, not_14_out, not_15_out;

  not not_1 (not_1_out, S2);
  and and_1 (and_1_out, not_1_out, S1, X);
  and and_2 (and_2_out, S2, not_2_out, not_3_out);
  not not_2 (not_2_out, S1);
  not not_3 (not_3_out, S0);
  and and_3 (and_3_out, S2, not_4_out, X);
  not not_4 (not_4_out, S1);
  and and_4 (and_4_out, S2, S1, S0);
  not not_5 (not_5_out, S2);
  and and_5 (and_5_out, not_5_out, not_6_out, X);
  not not_6 (not_6_out, S1);
  not not_7 (not_7_out, S2);
  and and_6 (and_6_out, not_7_out, S0, not_8_out);
  not not_8 (not_8_out, X);
  not not_9 (not_9_out, S0);
  and and_7 (and_7_out, S2, not_9_out, not_10_out);
  not not_10 (not_10_out, X);
  and and_8 (and_8_out, S2, S1);
  not not_11 (not_11_out, S2);
  and and_9 (and_9_out, not_11_out, not_12_out);
  not not_12 (not_12_out, X);
  and and_10 (and_10_out, S0, not_13_out);
  not not_13 (not_13_out, X);
  and and_11 (and_11_out, S1, not_14_out);
  not not_14 (not_14_out, X);
  and and_12 (and_12_out, S1, S0);
  and and_13 (and_13_out, S2, S0, X);
  and and_14 (and_14_out, S2, S1, not_15_out);
  not not_15 (not_15_out, X);
  or or_1 (S2T, and_1_out, and_2_out, and_3_out, and_4_out);
  or or_2 (S1T, and_5_out, and_6_out, and_7_out, and_8_out);
  or or_3 (S0T, and_9_out, and_10_out, and_11_out, and_12_out);
  or or_4 (Y, and_13_out, and_14_out);
endmodule

module TempCirc1 (
  input  S2,
  input  S1,
  input  S0,
  input  X,
  output JS2,
  output KS2,
  output JS1,
  output KS1,
  output JS0,
  output KS0,
  output Y
);

  wire and_3_out, and_4_out, and_5_out, and_6_out, and_7_out, and_8_out, and_9_out, not_1_out, not_2_out,
       not_3_out, not_4_out, not_5_out, not_6_out, not_7_out, not_8_out, not_9_out;

  and and_1 (JS2, S1, S0, not_1_out);
  not not_1 (not_1_out, X);
  and and_2 (KS2, S1, S0, not_2_out);
  not not_2 (not_2_out, X);
  and and_3 (and_3_out, S0, not_3_out);
  not not_3 (not_3_out, X);
  not not_4 (not_4_out, S1);
  and and_4 (and_4_out, not_4_out, not_5_out);
  not not_5 (not_5_out, X);
  and and_5 (and_5_out, S1, X);
  not not_6 (not_6_out, S2);
  not not_7 (not_7_out, X);
  not not_8 (not_8_out, S1);
  not not_9 (not_9_out, S0);
  or or_1 (JS1, and_3_out, S1);
  or or_2 (JS0, and_4_out, and_5_out);
  and and_6 (and_6_out, not_6_out, S1, S0, not_7_out);
  and and_7 (and_7_out, S2, not_8_out);
  and and_8 (and_8_out, S2, not_9_out);
  and and_9 (and_9_out, S2, X);
  or or_3 (Y, and_6_out, and_7_out, and_8_out, and_9_out);

  assign KS0 = 1'b1;
  assign KS1 = S0;
endmodule
