// Logisim project ETY_TM8_AkmalRamadhan_2206081534.circ as structural Verilog: 1 circuit, main circuit Nomor 3
module Nomor_3 (
  input  E
);

  wire and_1_out, and_2_out, and_3_out, clock_1_out, or_1_out, S0_q, S1_q, xor_1_out;

  Clock clock_1 (.out(clock_1_out));
  and and_1 (and_1_out, ~S1_q, ~S0_q, E);  // AND_Gate
  and and_2 (and_2_out, S1_q, ~E);  // AND_Gate
  and and_3 (and_3_out, S1_q, S0_q);
  or or_1 (or_1_out, and_1_out, and_2_out, and_3_out);
  xor xor_1 (xor_1_out, S0_q, E);
  D_Flip_Flop S1 (.clk(clock_1_out), .D(or_1_out), .Q(S1_q));  // open: Qn, preset, en, reset
  D_Flip_Flop S0 (.clk(clock_1_out), .D(xor_1_out), .Q(S0_q));  // open: Qn, preset, en, reset
endmodule
